# Fritzing sketch voltmetre (saved by Fritzing 1.0.3b)
breadboards: 1

parts:
  Raspberry_Pi_1 = Raspberry Pi 4 [part_number=RPI-4-b]
  Composant1 = Adafruit ADS1115 16Bit I2C ADC [part_number="Adafruit #1085"]
  OLED1 = SSD1306 0.96in 128x64 I2C Monochrome OLED Display
  R1 = Resistor [tolerance=±5% power=0.25W resistance=4.7k package=THT]
  R2 = Resistor [tolerance=±5% power=0.25W resistance=47k package=THT]
  VCC1 = Battery [internal_resistance=0.1Ω]

nets:
  3V3: Raspberry_Pi_1.3v3, Composant1.VDD, OLED1.VCC, R1.Pin_0, R2.Pin_0
  N1: Raspberry_Pi_1.GPIO2, Raspberry_Pi_1.GPIO27, Raspberry_Pi_1.GPIO11, Composant1.SDA, OLED1.SDA, R1.Pin_1
  N2: Raspberry_Pi_1.GPIO3, Composant1.SCL, OLED1.SCL, R2.Pin_1
  GND: Raspberry_Pi_1.GND, Composant1.GND, OLED1.GND, VCC1.-
  N3: Composant1.AIN0, VCC1.+

custom parts:
  Raspberry Pi 4: The RPi4, a faster version of the awesome Raspberry Pi 2 B ARM Board with 40 pin gpio. Ready for special Raspberry Pi B+ and RPi2 Hat (Hardware attached (on) top)
  Adafruit ADS1115 16Bit I2C ADC: For microcontrollers without an analog-to-digital converter or when you want a higher-precision ADC, the ADS1115 provides 16-bit precision at 860 samples/second over I2C. The chip can be configured as 4 single-ended input channels, or two differential channels. As a nice bonus, it even includes a programmable gain amplifier, up to x16, to help boost up smaller single/differential signals to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
